# Fritzing sketch deskinator-wiring (saved by Fritzing 1.0.5)
breadboards: 2

parts:
  IMU = Adafruit BNO085 9-DOF Orientation IMU Fusion [part_number="Addfruit #4754"]
  NEMA17-1 = Stepper Motor - Bipolar
  NEMA17-2 = Stepper Motor - Bipolar
  RBPi = Raspberry Pi 4B
  Lipo = 4S Li-ion/LiPo 14.8 V XT60 [package=lipo-2000]
  Vacuum-DC = DC Vacuum Fan 12V
  Driver-Left = TMC2209 [package=THT]
  Driver-Right = TMC2209 [package=THT]
  LEFT = Adafruit APDS9960 Proximity Sensor [part_number="Adafruit #3595"]
  RIGHT = Adafruit APDS9960 Proximity Sensor [part_number="Adafruit #3595"]
  Buzzer = Piezo Speaker
  GESTURE = Adafruit APDS9960 Proximity Sensor [part_number="Adafruit #3595"]
  Q1 = MOSFET-NCHANNEL [package=to220v]
  100Ω-Res = 10kΩ Resistor [package="0402 [SMD]"]
  10kΩ-Res = 10kΩ Resistor [package="0402 [SMD]"]
  Q2 = MOSFET-NCHANNEL [package=to220v]
  D1 = Rectifier Diode [part_number=1N4001 package="300 mil [THT]"]
  XL4015-5_1V = DC_DC_XL4015 [package=board_screw]

nets:
  N1: IMU.SCL/SCK/RX, RBPi.GPIO13
  N2: IMU.SDA/MISO/TX, RBPi.GPIO6
  N3: NEMA17-1.A, Driver-Left.M1B
  N4: NEMA17-1.C, Driver-Left.M1A
  N5: NEMA17-1.B, Driver-Left.M2A
  N6: NEMA17-1.D, Driver-Left.M2B
  N7: NEMA17-2.A, Driver-Right.M1B
  N8: NEMA17-2.C, Driver-Right.M1A
  N9: NEMA17-2.B, Driver-Right.M2A
  N10: NEMA17-2.D, Driver-Right.M2B
  N11: RBPi.5V, Buzzer.pin2, XL4015-5_1V.OUT+
  N12: RBPi.GPIO2, GESTURE.SDA
  N13: RBPi.GPIO3, GESTURE.SCL
  GND: RBPi.GND, Lipo.-, Driver-Left.GND, Driver-Right.GND, LEFT.GND, RIGHT.GND, GESTURE.GND, Q1.S, 10kΩ-Res.Pin_1, Q2.S, XL4015-5_1V.IN-, XL4015-5_1V.OUT-
  N14: RBPi.GPIO27, RBPi.GPIO16, Driver-Left.EN, Driver-Right.EN
  N15: RBPi.GPIO22, Driver-Right.Step
  N16: RBPi.GPIO23, Driver-Right.Dir
  N17: RBPi.GPIO24, RIGHT.SCL
  N18: RBPi.GPIO25, RIGHT.SDA
  N19: RBPi.GPIO5, 100Ω-Res.Pin_0
  N20: RBPi.GPIO12, Q2.G
  N21: RBPi.GPIO19, LEFT.SDA
  N22: RBPi.GPIO26, LEFT.SCL
  N23: RBPi.GPIO20, Driver-Left.Step
  N24: RBPi.GPIO21, Driver-Left.Dir
  N25: Lipo.+, Vacuum-DC.pin_1, Driver-Left.VM, Driver-Right.VM, D1.cathode, XL4015-5_1V.IN+
  N26: Vacuum-DC.pin_2, Q1.D, D1.anode
  N27: Buzzer.pin1, Q2.D
  N28: Q1.G, 100Ω-Res.Pin_1, 10kΩ-Res.Pin_0

notes:
  12V
  5.10V

custom parts:
  4S Li-ion/LiPo 14.8 V XT60: 4S Li-ion/LiPo pack, 14.8 V nominal (16.8 V full), XT60 connector.
  DC Vacuum Fan 12V: DC Vacuum Fan
  TMC2209: TMC2209-LA stepper motor controller and driver. Supply voltage 4.75-28V Iphase up to 1.77A rms (2.5A peak)
  Adafruit APDS9960 Proximity Sensor: This breakout is chock full o' sensors! Add basic gesture sensing, RGB color sensing, proximity sensing, or ambient light sensing to your project with the Adafruit APDS9960 Proximity, Light, RGB and Gesture Sensor. When connected to your microcontroller (running our library code) it can detect simple gestures (left to right, right to left, up to down, down to up are currently supported),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
  10kΩ Resistor: Resistor Basic schematic elements and footprints for 0603, 1206, and PTH resistors.
  DC_DC_XL4015: DC-DC Converter step down voltage regulator XL4016 custom sketch.
